# Fritzing sketch BoxOfTricks (saved by Fritzing 1.0.6)
breadboards: 1

parts:
  Part1 = Logic Level Converter
  A1 = Raspberry Pi 5
  T0_framing_signal_0-5_V = 2.1mm male with Terminal Block
  ADC1 = MCP3008 [package=dil16]
  sample_environment_signal_-10_to_10_V = 2.1mm male with Terminal Block
  R1 = Resistor [tolerance=±5% power=0.25W resistance=8k package=THT]
  R2 = Resistor [tolerance=±5% power=0.25W resistance=18k package=THT]
  A3 = u-blox NEO-7M GPS Breakout

nets:
  GND: Part1.GND, A1.GND, T0_framing_signal_0-5_V.NEG, ADC1.DGND, ADC1.AGND, sample_environment_signal_-10_to_10_V.NEG, R1.Pin_0, A3.Pin_2
  3V3: Part1.LV, A1.3V3, ADC1.VREF, ADC1.VDD, A3.Pin_1
  N1: Part1.RX_LV, A1.GPIO17
  N2: Part1.RX_HV, T0_framing_signal_0-5_V.POS
  N3: Part1.HV, A1.5V
  N4: A1.GPIO14, A3.Pin_4
  N5: A1.GPIO15, A3.Pin_3
  N6: A1.GPIO18, A3.Pin_5
  N7: A1.GPIO22, ADC1.CS/SHDN
  N8: A1.GPIO10, ADC1.Din
  N9: A1.GPIO9, ADC1.Dout
  N10: A1.GPIO11, ADC1.CLK
  N11: ADC1.CH0, R1.Pin_1, R2.Pin_1
  N12: sample_environment_signal_-10_to_10_V.POS, R2.Pin_0

custom parts:
  Raspberry Pi 5: The RPi5, a faster version of the awesome Raspberry Pi4B ARM Board with 40 pin gpio.
  2.1mm male with Terminal Block: 2.1mm male with Terminal Block based on work by John De Cristofaro
